// Logisim project GT-2200.circ as structural Verilog: 4 circuits, main circuit my circuit
module my_circuit (
  output [31:0] out_1
);

  wire Clock, CmpOut, comparison_logic_1_comp_logic, DrALU, DrMEM, DrOFF, DrPC, DrReg, LdA, LdB, LdCmp, LdIR,
       LdMAR, LdPC, WrMEM, WrReg;
  wire [1:0] ALU, OP_Chk, RegSel;
  wire [3:0] regno;
  wire [5:0] multiplexer_2_out, next, Next_q, rom_2_data, rom_3_data;
  wire [23:0] MAR_q;
  wire [31:0] A_q, alu_1_out_4, B_q, IR, PC_q, ram_1_data, reg_1_dout;

  Clock clock_1 (.out(Clock));
  Register #(.width(32)) PC (.D(out_1), .en(LdPC), .Q(PC_q), .clk(Clock), .clr(1'b0));
  assign out_1 = DrPC ? PC_q : 32'bz;  // Controlled_Buffer controlled_buffer_1
  Register #(.width(32)) A (.D(out_1), .en(LdA), .Q(A_q), .clk(Clock), .clr(1'b0));
  assign out_1 = DrALU ? alu_1_out_4 : 32'bz;  // Controlled_Buffer controlled_buffer_2
  Register #(.width(6)) u_Next (.D(multiplexer_2_out), .en(1'b1), .Q(Next_q), .clk(Clock), .clr(1'b0));
  Register #(.width(32)) B (.D(out_1), .en(LdB), .Q(B_q), .clk(Clock), .clr(1'b0));
  ALU alu_1 (.A(A_q), .B(B_q), .SEL(ALU), .out_4(alu_1_out_4));
  Reg reg_1 (.WrReg(WrReg), .Clock(Clock), .regno(regno), .Din(out_1), .Dout(reg_1_dout));
  assign out_1 = DrReg ? reg_1_dout : 32'bz;  // Controlled_Buffer controlled_buffer_3
  ROM #(.addrWidth(6), .dataWidth(25)) rom_1 (
    .addr(Next_q),
    .data({OP_Chk, ALU, RegSel, WrMEM, WrReg, LdCmp, LdB, LdA, LdMAR, LdIR, LdPC, DrOFF, DrPC, DrALU, DrMEM, DrReg, next}),
    .sel(1'b1));
  assign out_1 = DrMEM ? ram_1_data : 32'bz;  // Controlled_Buffer controlled_buffer_4
  Comparison_Logic comparison_logic_1 (.Bus(out_1), .IR(IR[27:24]), .Comp_Logic(comparison_logic_1_comp_logic));
  Register #(.width(24)) MAR (.D(out_1[23:0]), .en(LdMAR), .Q(MAR_q), .clk(Clock), .clr(1'b0));
  Register #(.width(32)) u_IR (.D(out_1), .en(LdIR), .Q(IR), .clk(Clock), .clr(1'b0));
  assign out_1 = DrOFF ? {{13{IR[19]}}, IR[18:0]} : 32'bz;  // Controlled_Buffer controlled_buffer_5
  Register #(.width(1), .trigger("falling")) CmpReg (
    .D(comparison_logic_1_comp_logic), .en(LdCmp), .Q(CmpOut), .clk(Clock), .clr(1'b0));
  RAM #(.addrWidth(24), .dataWidth(32), .bus("separate")) ram_1 (
    .addr(MAR_q), .din(out_1), .data(ram_1_data), .str(WrMEM), .sel(1'b1), .clk(Clock), .ld(1'b1), .clr(1'b0));
  Multiplexer #(.select(2), .width(4), .disabled(0), .enable("false")) multiplexer_1 (
    .in0(IR[27:24]), .in1(IR[23:20]), .in2(IR[3:0]), .in3(IR[3:0]), .out(regno), .sel(RegSel));
  ROM #(.addrWidth(4), .dataWidth(6)) rom_2 (.addr(IR[31:28]), .data(rom_2_data), .sel(1'b1));
  ROM #(.addrWidth(2), .dataWidth(6)) rom_3 (.addr({1'b0, CmpOut}), .data(rom_3_data), .sel(1'b1));
  Multiplexer #(.select(2), .width(6), .disabled(0), .enable("false")) multiplexer_2 (
    .in0(next), .in1(rom_2_data), .in2(rom_3_data), .out(multiplexer_2_out), .sel(OP_Chk));  // open: in3

  // Other names for the same wires on the sheet: RZ[3:0] = IR[3:0]; RY[3:0] = IR[23:20]; RX[3:0] = IR[27:24];
  //   OP[3:0] = IR[31:28]

  // Notes on the sheet:
  //   contents of rom_1 (hex, n*v repeats v):
  //   6201 1082 e00900 84044 108045 20100 84047 8408 20100 8404a 10804b 420100 8404d 10804e 121010f 4210
  //   600900 4212 8413 900 4215 8416 20100 84058 8419 211a 20080 8405c 841d 211e 40040 a0220 840 21
  //   unused
  //   contents of rom_2 (hex, n*v repeats v):
  //   3 6 9 c 11 14 0 0 17 1b 0 0 1f 0 0 21
  //   contents of rom_3 (hex, n*v repeats v):
  //   0 f
endmodule

module ALU (
  input  [31:0] A,
  input  [31:0] B,
  input  [1:0] SEL,
  output [31:0] out_4
);

  wire [31:0] ADD, INC, NAND, SUB;

  Adder #(.width(32)) adder_1 (.a(A), .b(B), .out(ADD));  // open: cin, cout
  Subtractor #(.width(32)) subtractor_1 (.a(A), .b(B), .out(SUB));  // open: bin, bout
  assign NAND = ~(A & B);  // NAND_Gate nand_1, 32 bits wide
  Adder #(.width(32)) adder_2 (.a(A), .b(32'h1), .out(INC));  // open: cin, cout
  Multiplexer #(.select(2), .width(32), .disabled(0), .enable("false")) multiplexer_1 (
    .in0(ADD), .in1(SUB), .in2(NAND), .in3(INC), .out(out_4), .sel(SEL));
endmodule

module Reg (
  input  WrReg,
  input  Clock,
  input  [3:0] regno,
  input  [31:0] Din,
  output [31:0] Dout
);

  wire _0, _1, _2, _3, _4, _5, _6, _7, _8, _9, _10, _11, _12, _13, _14, _15, Clk;
  wire [3:0] and_2_out;
  wire [31:0] D1, D2, D3, D4, D5, D6, D7, D8, D9, D10, D11, D12, D13, D14, D15, register_1_q, register_2_q,
       register_3_q, register_4_q, register_5_q, register_6_q, register_7_q, register_8_q, register_9_q,
       register_10_q, register_11_q, register_12_q, register_13_q, register_14_q, register_15_q,
       register_16_q;

  Decoder #(.select(4), .enable("false")) decoder_1 (
    .out0(_0), .out1(_1), .out2(_2), .out3(_3), .out4(_4), .out5(_5), .out6(_6), .out7(_7), .out8(_8),
    .out9(_9), .out10(_10), .out11(_11), .out12(_12), .out13(_13), .out14(_14), .out15(_15), .sel(regno));
  and and_1 (Clk, WrReg, Clock);
  assign and_2_out = {4{Clock}} & regno;  // AND_Gate and_2, 4 bits wide
  Demultiplexer #(.select(4), .width(32), .disabled(0), .enable("false")) demultiplexer_1 (
    .out1(D1), .out2(D2), .out3(D3), .out4(D4), .out5(D5), .out6(D6), .out7(D7), .out8(D8), .out9(D9),
    .out10(D10), .out11(D11), .out12(D12), .out13(D13), .out14(D14), .out15(D15), .in(Din), .sel(and_2_out));  // open: out0
  Register #(.width(32), .trigger("falling")) register_1 (
    .D({32{1'b0}}), .en(_0), .Q(register_1_q), .clk(Clk), .clr(1'b1));
  Register #(.width(32), .trigger("falling")) register_2 (.D(D1), .en(_1), .Q(register_2_q), .clk(Clk), .clr(1'b0));
  Register #(.width(32), .trigger("falling")) register_3 (.D(D2), .en(_2), .Q(register_3_q), .clk(Clk), .clr(1'b0));
  Register #(.width(32), .trigger("falling")) register_4 (.D(D3), .en(_3), .Q(register_4_q), .clk(Clk), .clr(1'b0));
  Register #(.width(32), .trigger("falling")) register_5 (.D(D4), .en(_4), .Q(register_5_q), .clk(Clk), .clr(1'b0));
  Register #(.width(32), .trigger("falling")) register_6 (.D(D5), .en(_5), .Q(register_6_q), .clk(Clk), .clr(1'b0));
  Register #(.width(32), .trigger("falling")) register_7 (.D(D6), .en(_6), .Q(register_7_q), .clk(Clk), .clr(1'b0));
  Register #(.width(32), .trigger("falling")) register_8 (.D(D7), .en(_7), .Q(register_8_q), .clk(Clk), .clr(1'b0));
  Register #(.width(32), .trigger("falling")) register_9 (.D(D8), .en(_8), .Q(register_9_q), .clk(Clk), .clr(1'b0));
  Register #(.width(32), .trigger("falling")) register_10 (.D(D9), .en(_9), .Q(register_10_q), .clk(Clk), .clr(1'b0));
  Register #(.width(32), .trigger("falling")) register_11 (.D(D10), .en(_10), .Q(register_11_q), .clk(Clk), .clr(1'b0));
  Register #(.width(32), .trigger("falling")) register_12 (.D(D11), .en(_11), .Q(register_12_q), .clk(Clk), .clr(1'b0));
  Register #(.width(32), .trigger("falling")) register_13 (.D(D12), .en(_12), .Q(register_13_q), .clk(Clk), .clr(1'b0));
  Register #(.width(32), .trigger("falling")) register_14 (.D(D13), .en(_13), .Q(register_14_q), .clk(Clk), .clr(1'b0));
  Register #(.width(32), .trigger("falling")) register_15 (.D(D14), .en(_14), .Q(register_15_q), .clk(Clk), .clr(1'b0));
  Register #(.width(32), .trigger("falling")) register_16 (.D(D15), .en(_15), .Q(register_16_q), .clk(Clk), .clr(1'b0));
  Multiplexer #(.select(4), .width(32), .disabled(0), .enable("false")) multiplexer_1 (
    .in0(register_1_q), .in1(register_2_q), .in2(register_3_q), .in3(register_4_q), .in4(register_5_q),
    .in5(register_6_q), .in6(register_7_q), .in7(register_8_q), .in8(register_9_q), .in9(register_10_q),
    .in10(register_11_q), .in11(register_12_q), .in12(register_13_q), .in13(register_14_q),
    .in14(register_15_q), .in15(register_16_q), .out(Dout), .sel(regno));
endmodule

module Comparison_Logic (
  input  [31:0] Bus,
  input  [3:0] IR,
  output Comp_Logic
);

  wire and_1_out, not_1_out, not_2_out, or_1_out, or_2_out;

  not not_1 (not_1_out, Bus[31]);
  or or_1 (or_1_out, Bus[0], Bus[1], Bus[2], Bus[3], Bus[4], Bus[5], Bus[6], Bus[7], Bus[8], Bus[9], Bus[10], Bus[11], Bus[12], Bus[13], Bus[14], Bus[15], Bus[16], Bus[17], Bus[18], Bus[19], Bus[20], Bus[21], Bus[22], Bus[23], Bus[24], Bus[25], Bus[26], Bus[27], Bus[28], Bus[29], Bus[30]);
  or or_2 (or_2_out, Bus[15], Bus[0], Bus[1], Bus[2], Bus[3], Bus[4], Bus[5], Bus[6], Bus[7], Bus[8], Bus[9], Bus[10], Bus[11], Bus[12], Bus[13], Bus[14], Bus[16], Bus[17], Bus[18], Bus[19], Bus[20], Bus[21], Bus[22], Bus[23], Bus[24], Bus[25], Bus[26], Bus[27], Bus[28], Bus[29], Bus[30], Bus[31]);
  and and_1 (and_1_out, or_1_out, not_1_out);
  not not_2 (not_2_out, or_2_out);
  Multiplexer #(.disabled(0), .enable("false")) multiplexer_1 (
    .in0(not_2_out), .in1(and_1_out), .out(Comp_Logic), .sel(IR[0]));
endmodule
